# Fritzing sketch Untitled Sketch (saved by Fritzing 0.9.3b)
breadboards: 1

parts:
  U1 = NodeMCU V3.0
  YwRobot_Power_Supply1 = YwRobot Breadboard Power Supply [part_number=545043]
  KY-1 = Keyes Relay [package=THT]

nets:
  N1: U1.3V3, KY-1.signal
  N2: U1.GND#6, U1.GND#13, U1.GND#16, U1.GND#33, YwRobot_Power_Supply1.GND#13, YwRobot_Power_Supply1.GND#14, KY-1.power
  N3: U1.D5, KY-1.ground
  N4: U1.Vin, YwRobot_Power_Supply1.VCC#9, YwRobot_Power_Supply1.VCC#10
  N5: YwRobot_Power_Supply1.VCC#5, YwRobot_Power_Supply1.VCC#6
  N6: YwRobot_Power_Supply1.GND#11, YwRobot_Power_Supply1.GND#12

notes:
  Relay sırasıyla;
  VCC GND IN
  Lamba
  220 V

custom parts:
  NodeMCU V3.0: ESP8266 based NodeMCU
  YwRobot Breadboard Power Supply: The YwRobot Breadboard Power Supply (MB-V2) has two power rails; they can be 5V or 3V3. Power to the module can be provided through the female USB socket or through the A10 (female) 2.1mm power jack.
  Keyes Relay: The Keyes 5V relay module is suitable for SCM development, home appliance control. It uses a 5V~12V TIL control signal which can control DC / AC signal.
